# Fritzing sketch BB-8 Sketch (saved by Fritzing 0.9.9b)
breadboards: 4

parts:
  ESP32_-_Back1 = ESP32 - CAM
  U1 = ESP32S-HiLetgo [part_number=ESP32S-HiLetgo]
  U2 = 74HC595 SMD [package="SO16 [SMD]"]
  M1 = RioRand LM2596
  LED1 = LED - 3mm [color="Red (633nm)" current=0.030 package="3 mm [THT]"]
  LED2 = LED - 3mm [color="Red (633nm)" current=0.030 package="3 mm [THT]"]
  LED3 = LED - 3mm [color="Red (633nm)" current=0.030 package="3 mm [THT]"]
  LED4 = LED - 3mm [color="Red (633nm)" current=0.030 package="3 mm [THT]"]
  Power_plug1 = Power plug
  S1 = Pololu DRV 8833 Dual Motor Driver Carrier [part_number=DRV8833]
  S1_1 = Pololu DRV 8833 Dual Motor Driver Carrier [part_number=DRV8833]  # not connected
  S1_2 = Pololu DRV 8833 Dual Motor Driver Carrier [part_number=DRV8833]  # not connected
  M2 = DC Motor  # not connected
  U3 = HALL-EFFECT [package=sc70]
  Mod1 = elechouse_voice_recognition_module_v3
  U4 = 74HC595 SMD [package="SO16 [SMD]"]
  U5 = 74HC595 SMD [package="SO16 [SMD]"]
  DFRobot_DFPlayer_Mini1 = DFRobot DFPlayer Mini [part_number=DFR0299]
  SP1 = SPEAKER [package=pcb_mount_speaker]
  LED6 = smd LED [color="Red (633nm)" package="0805 [SMD]"]
  LED7 = smd LED [color="Red (633nm)" package="0805 [SMD]"]
  LED8 = smd LED [color="Red (633nm)" package="0805 [SMD]"]
  LED9 = smd LED [color="Red (633nm)" package="0805 [SMD]"]
  LED10 = smd LED [color="Red (633nm)" package="0805 [SMD]"]
  LED11 = smd LED [color="Red (633nm)" package="0805 [SMD]"]
  LED12 = smd LED [color="Red (633nm)" package="0805 [SMD]"]
  LED13 = smd LED [color="Red (633nm)" package="0805 [SMD]"]
  LED14 = smd LED [color="Red (633nm)" package="0805 [SMD]"]
  LED15 = smd LED [color="Red (633nm)" package="0805 [SMD]"]
  LED16 = smd LED [color="Red (633nm)" package="0805 [SMD]"]
  LED17 = smd LED [color="Red (633nm)" package="0805 [SMD]"]
  LED18 = smd LED [color="Red (633nm)" package="0805 [SMD]"]
  LED19 = smd LED [color="Red (633nm)" package="0805 [SMD]"]
  LED20 = smd LED [color="Red (633nm)" package="0805 [SMD]"]
  LED21 = smd LED [color="Red (633nm)" package="0805 [SMD]"]
  LED5 = smd LED [color="Red (633nm)" package="0805 [SMD]"]

nets:
  N1: ESP32_-_Back1.GPIO2, U2.DS
  N2: ESP32_-_Back1.GPIO14, U1.GPIO19
  N3: ESP32_-_Back1.GPIO15, U1.GPIO18
  N4: ESP32_-_Back1.GPIO13, U2.SH_CP
  N5: ESP32_-_Back1.GPIO12, U2.ST_CP
  GND: ESP32_-_Back1.GND, M1.Pin_2, Power_plug1.GND, S1.GND, U3.GND, Mod1.GND, U4.OE, U5.OE, DFRobot_DFPlayer_Mini1.GND-1
  VCC: ESP32_-_Back1.5V, U1.VIN, M1.Pin_1, Power_plug1.VCC, S1.VIN, U3.VCC, Mod1.VCC, DFRobot_DFPlayer_Mini1.VCC
  N6: U1.GPIO36, U3.OUT
  N7: U1.GPIO32, DFRobot_DFPlayer_Mini1.RX
  N8: U1.GPIO33, DFRobot_DFPlayer_Mini1.TX
  N9: U1.GPIO25, U5.DS
  N10: U1.GPIO26, U4.ST_CP, U5.ST_CP
  N11: U1.GPIO27, U4.SH_CP, U5.SH_CP
  N12: U1.GND, LED5.cathode
  N13: U1.GPIO13, LED5.anode
  N14: U1.GPIO16, Mod1.RXD
  N15: U1.GPIO17, Mod1.TXD
  N16: U1.GPIO22, S1.connector6
  N17: U1.GPIO23, S1.connector5
  N18: U2.Q1, LED2.anode
  N19: U2.Q2, LED3.anode
  N20: U2.Q3, LED4.anode
  VCC_2: U2.MR, U2.VCC, M1.Pin_3, U4.MR, U4.VCC, U5.MR, U5.VCC
  N21: U2.OE, M1.Pin_4, LED1.cathode, LED2.cathode, LED3.cathode, LED4.cathode
  N22: U2.Q0, LED1.anode
  N23: U4.Q1, LED17.anode
  N24: U4.Q2, LED19.anode
  N25: U4.Q3, LED18.anode
  N26: U4.Q4, LED14.anode
  N27: U4.Q5, LED16.anode
  N28: U4.Q6, LED20.anode
  N29: U4.Q7, LED21.anode
  N30: U4.DS, U5.Q7'
  N31: U4.Q0, LED15.anode
  N32: U5.Q1, LED13.anode
  N33: U5.Q2, LED10.anode
  N34: U5.Q3, LED11.anode
  N35: U5.Q4, LED8.anode
  N36: U5.Q5, LED9.anode
  N37: U5.Q6, LED7.anode
  N38: U5.Q7, LED6.anode
  N39: U5.Q0, LED12.anode
  N40: DFRobot_DFPlayer_Mini1.SPK_1, SP1.-
  N41: DFRobot_DFPlayer_Mini1.SPK_2, SP1.+
  N42: LED6.cathode, LED7.cathode, LED8.cathode, LED9.cathode, LED10.cathode, LED11.cathode, LED12.cathode, LED13.cathode, LED14.cathode, LED15.cathode, LED16.cathode, LED17.cathode, LED18.cathode, LED19.cathode, LED20.cathode, LED21.cathode

notes:
  5V Input
  5V -> 3V Step Down

custom parts:
  ESP32 - CAM: The ESP32-CAM has a very competitive small-size camera module that can operate independently as a minimum system with a footprint of only 27*40.5*4.5mm and a deep sleep current of up to 6mA.
  ESP32S-HiLetgo: HiLetgo ESP-WROOM-32 ESP32 ESP-32S Development Board 2.4GHz Dual-Mode WiFi + Bluetooth Dual Cores Microcontroller The ESP32 integrated with Antenna switches, RF Balun, power amplifiers, low-noise amplifiers, filters, and management modules, and the entire solution occupies the least area of PCB. 2.4 GHz Wi-Fi plus Bluetooth dual-mode chip, with TSMC Ultra-low power consumption 40nm technology,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
  elechouse_voice_recognition_module_v3: Elechouse voice recognition module v3. Module that accepts up to 7 voice commands via a microphone. Note: currently this part was made from a .png image of the board. Thus the pcb is probably not correctly dimensioned since the input data was not precise. Before making boards based on this part, print out the footprint and check it (and provide corrections via the Fritzing forums to correct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
